# Fritzing sketch SensorManagement (saved by Fritzing 0.9.3b)

parts:
  M1 = DOIT Esp32 DevKit v1 (30 pins long, 11 pins width) [part_number=ESP32S-PIN30]
  A1 = tf-luna lidar
  A2 = tf-luna lidar
  Raspberry_Pi_1 = Raspberry Pi 4 [part_number=RPI-4-b]
  USBTTL1 = USB A Plug  # not connected
  Power_plug1 = USB-C plug  # not connected
  A3 = tf-luna lidar
  A4 = tf-luna lidar

nets:
  N1: M1.GND, A1.Pin_4, A2.Pin_4, A3.Pin_4, A4.Pin_5
  N2: M1.D19, A1.Pin_2
  N3: M1.D21, A1.Pin_3
  N4: M1.D22, A2.Pin_2
  N5: M1.D23, A2.Pin_3
  N6: M1.VIN, A1.Pin_1, A2.Pin_1, A3.Pin_1, A4.Pin_1
  N7: Raspberry_Pi_1.GPIO15, A3.Pin_3
  N8: Raspberry_Pi_1.GPIO14, A3.Pin_2

custom parts:
  DOIT Esp32 DevKit v1 (30 pins long, 11 pins width): The DOIT Esp32 DevKit v1 is one of the development board created by DOIT to evaluate the ESP-WROOM-32 module. It is based on the ESP32 microcontroller that boasts Wifi, Bluetooth, Ethernet and Low Power support all in a single chip. (vanepp) made breadboard work, adjusted pin numbering and labels and reduced size of schematic and cleaned up pcb. This chip is 30pins long (2 x15) and 11 pins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
  tf-luna lidar: TF-Luna is using Time of Flight (TOF) principle to measure distance, and it periodically emits near infrared modulated wave.
  Raspberry Pi 4: The RPi4, a faster version of the awesome Raspberry Pi 2 B ARM Board with 40 pin gpio. Ready for special Raspberry Pi B+ and RPi2 Hat (Hardware attached (on) top)
  USB A Plug: USB A Plug breadboard only for documetnation purposes.
  USB-C plug: power plug
